// Logisim project main.circ as structural Verilog: 5 circuits, main circuit main
module main (
  input  Hold
);

  wire \bit , cdm16e_1_p2, cdm16e_1_p5, cdm16e_1_p6, cdm16e_1_p7, cdm16e_1_p8, cdm16e_1_p9, cdm16e_1_p10,
       cdm16e_1_p11, cdm16e_1_p12, cdm16e_1_p13, cl, mem, not_1_out, r_w, screen_mem_1_clock_out,
       screen_mem_2_clock_out, screen_mem_3_clock_out, screen_mem_4_clock_out;
  wire [15:0] addr, cdm16e_1_p18, cdm16e_1_p19, data, np1, np2, np3, r1, screen_mem_1__14,
       screen_mem_1__14_2, screen_mem_1_addr_out, screen_mem_1_data_out, screen_mem_1_next_pos,
       screen_mem_1_str0, screen_mem_1_str0_2, screen_mem_1_str1, screen_mem_1_str1_2, screen_mem_1_str2,
       screen_mem_1_str2_2, screen_mem_1_str3, screen_mem_1_str3_2, screen_mem_1_str4, screen_mem_1_str4_2,
       screen_mem_1_str5, screen_mem_1_str5_2, screen_mem_1_str6, screen_mem_1_str6_2, screen_mem_1_str7,
       screen_mem_1_str7_2, screen_mem_1_str8, screen_mem_1_str8_2, screen_mem_1_str9, screen_mem_1_str9_2,
       screen_mem_1_str10, screen_mem_1_str10_2, screen_mem_1_str11, screen_mem_1_str11_2,
       screen_mem_1_str12, screen_mem_1_str12_2, screen_mem_1_str13, screen_mem_1_str13_2,
       screen_mem_1_str15, screen_mem_1_str15_2, screen_mem_2__14, screen_mem_2__14_2, screen_mem_2_addr_out,
       screen_mem_2_data_out, screen_mem_2_next_pos, screen_mem_2_str0, screen_mem_2_str0_2,
       screen_mem_2_str1, screen_mem_2_str1_2, screen_mem_2_str2, screen_mem_2_str2_2, screen_mem_2_str3,
       screen_mem_2_str3_2, screen_mem_2_str4, screen_mem_2_str4_2, screen_mem_2_str5, screen_mem_2_str5_2,
       screen_mem_2_str6, screen_mem_2_str6_2, screen_mem_2_str7, screen_mem_2_str7_2, screen_mem_2_str8,
       screen_mem_2_str8_2, screen_mem_2_str9, screen_mem_2_str9_2, screen_mem_2_str10, screen_mem_2_str10_2,
       screen_mem_2_str11, screen_mem_2_str11_2, screen_mem_2_str12, screen_mem_2_str12_2,
       screen_mem_2_str13, screen_mem_2_str13_2, screen_mem_2_str15, screen_mem_2_str15_2, screen_mem_3__14,
       screen_mem_3__14_2, screen_mem_3_addr_out, screen_mem_3_data_out, screen_mem_3_next_pos,
       screen_mem_3_str0, screen_mem_3_str0_2, screen_mem_3_str1, screen_mem_3_str1_2, screen_mem_3_str2,
       screen_mem_3_str2_2, screen_mem_3_str3, screen_mem_3_str3_2, screen_mem_3_str4, screen_mem_3_str4_2,
       screen_mem_3_str5, screen_mem_3_str5_2, screen_mem_3_str6, screen_mem_3_str6_2, screen_mem_3_str7,
       screen_mem_3_str7_2, screen_mem_3_str8, screen_mem_3_str8_2, screen_mem_3_str9, screen_mem_3_str9_2,
       screen_mem_3_str10, screen_mem_3_str10_2, screen_mem_3_str11, screen_mem_3_str11_2,
       screen_mem_3_str12, screen_mem_3_str12_2, screen_mem_3_str13, screen_mem_3_str13_2,
       screen_mem_3_str15, screen_mem_3_str15_2, screen_mem_4__14, screen_mem_4__14_2, screen_mem_4_addr_out,
       screen_mem_4_data_out, screen_mem_4_next_pos, screen_mem_4_str0, screen_mem_4_str0_2,
       screen_mem_4_str1, screen_mem_4_str1_2, screen_mem_4_str2, screen_mem_4_str2_2, screen_mem_4_str3,
       screen_mem_4_str3_2, screen_mem_4_str4, screen_mem_4_str4_2, screen_mem_4_str5, screen_mem_4_str5_2,
       screen_mem_4_str6, screen_mem_4_str6_2, screen_mem_4_str7, screen_mem_4_str7_2, screen_mem_4_str8,
       screen_mem_4_str8_2, screen_mem_4_str9, screen_mem_4_str9_2, screen_mem_4_str10, screen_mem_4_str10_2,
       screen_mem_4_str11, screen_mem_4_str11_2, screen_mem_4_str12, screen_mem_4_str12_2,
       screen_mem_4_str13, screen_mem_4_str13_2, screen_mem_4_str15, screen_mem_4_str15_2, screen_mem_5__14,
       screen_mem_5__14_2, screen_mem_5_str0, screen_mem_5_str0_2, screen_mem_5_str1, screen_mem_5_str1_2,
       screen_mem_5_str2, screen_mem_5_str2_2, screen_mem_5_str3, screen_mem_5_str3_2, screen_mem_5_str4,
       screen_mem_5_str4_2, screen_mem_5_str5, screen_mem_5_str5_2, screen_mem_5_str6, screen_mem_5_str6_2,
       screen_mem_5_str7, screen_mem_5_str7_2, screen_mem_5_str8, screen_mem_5_str8_2, screen_mem_5_str9,
       screen_mem_5_str9_2, screen_mem_5_str10, screen_mem_5_str10_2, screen_mem_5_str11,
       screen_mem_5_str11_2, screen_mem_5_str12, screen_mem_5_str12_2, screen_mem_5_str13,
       screen_mem_5_str13_2, screen_mem_5_str15, screen_mem_5_str15_2, screen_mem_6__14, screen_mem_6__14_2,
       screen_mem_6_str0, screen_mem_6_str0_2, screen_mem_6_str1, screen_mem_6_str1_2, screen_mem_6_str2,
       screen_mem_6_str2_2, screen_mem_6_str3, screen_mem_6_str3_2, screen_mem_6_str4, screen_mem_6_str4_2,
       screen_mem_6_str5, screen_mem_6_str5_2, screen_mem_6_str6, screen_mem_6_str6_2, screen_mem_6_str7,
       screen_mem_6_str7_2, screen_mem_6_str8, screen_mem_6_str8_2, screen_mem_6_str9, screen_mem_6_str9_2,
       screen_mem_6_str10, screen_mem_6_str10_2, screen_mem_6_str11, screen_mem_6_str11_2,
       screen_mem_6_str12, screen_mem_6_str12_2, screen_mem_6_str13, screen_mem_6_str13_2,
       screen_mem_6_str15, screen_mem_6_str15_2, screen_mem_7__14, screen_mem_7__14_2, screen_mem_7_str0,
       screen_mem_7_str0_2, screen_mem_7_str1, screen_mem_7_str1_2, screen_mem_7_str2, screen_mem_7_str2_2,
       screen_mem_7_str3, screen_mem_7_str3_2, screen_mem_7_str4, screen_mem_7_str4_2, screen_mem_7_str5,
       screen_mem_7_str5_2, screen_mem_7_str6, screen_mem_7_str6_2, screen_mem_7_str7, screen_mem_7_str7_2,
       screen_mem_7_str8, screen_mem_7_str8_2, screen_mem_7_str9, screen_mem_7_str9_2, screen_mem_7_str10,
       screen_mem_7_str10_2, screen_mem_7_str11, screen_mem_7_str11_2, screen_mem_7_str12,
       screen_mem_7_str12_2, screen_mem_7_str13, screen_mem_7_str13_2, screen_mem_7_str15,
       screen_mem_7_str15_2, screen_mem_8__14, screen_mem_8__14_2, screen_mem_8_str0, screen_mem_8_str0_2,
       screen_mem_8_str1, screen_mem_8_str1_2, screen_mem_8_str2, screen_mem_8_str2_2, screen_mem_8_str3,
       screen_mem_8_str3_2, screen_mem_8_str4, screen_mem_8_str4_2, screen_mem_8_str5, screen_mem_8_str5_2,
       screen_mem_8_str6, screen_mem_8_str6_2, screen_mem_8_str7, screen_mem_8_str7_2, screen_mem_8_str8,
       screen_mem_8_str8_2, screen_mem_8_str9, screen_mem_8_str9_2, screen_mem_8_str10, screen_mem_8_str10_2,
       screen_mem_8_str11, screen_mem_8_str11_2, screen_mem_8_str12, screen_mem_8_str12_2,
       screen_mem_8_str13, screen_mem_8_str13_2, screen_mem_8_str15, screen_mem_8_str15_2;

  // Probe on cdm16e_1_p2
  // Probe on cdm16e_1_p2
  // Probe on cdm16e_1_p2
  Clock clock_1 (.out(cl));
  // Probe on r1
  // Probe on r1
  // Probe on r1
  // Probe on cdm16e_1_p5
  // Probe on cdm16e_1_p5
  // Probe on cdm16e_1_p5
  // cdm16e cdm16e_1: pin names not known; wires that end beside it: Hold, cdm16e_1_p2, r1, cl, cdm16e_1_p5, cdm16e_1_p6, cdm16e_1_p7, cdm16e_1_p8, cdm16e_1_p9, cdm16e_1_p10, cdm16e_1_p11, cdm16e_1_p12, cdm16e_1_p13, mem, r_w, \bit , addr, cdm16e_1_p18, cdm16e_1_p19
  // Probe on data
  // Probe on data
  // Probe on data
  // Probe on data
  // Probe on addr
  // Probe on addr
  // Probe on addr
  // Probe on addr
  // Probe on cdm16e_1_p6
  // Probe on cdm16e_1_p6
  // Probe on cdm16e_1_p6
  assign data = not_1_out ? cdm16e_1_p18 : 16'bz;  // Controlled_Buffer controlled_buffer_1
  not not_1 (not_1_out, r_w);
  assign cdm16e_1_p19 = r_w ? data : 16'bz;  // Controlled_Buffer controlled_buffer_2
  // Probe on cdm16e_1_p7
  // Probe on cdm16e_1_p7
  // Probe on cdm16e_1_p7
  // Probe on cdm16e_1_p8
  // Probe on cdm16e_1_p8
  // Probe on cdm16e_1_p8
  DotMatrix #(.matrixcols(32), .matrixrows(16)) dotmatrix_1 (
    .col0(screen_mem_1_str0), .col1(screen_mem_1_str1), .col2(screen_mem_1_str2), .col3(screen_mem_1_str3),
    .col4(screen_mem_1_str4), .col5(screen_mem_1_str5), .col6(screen_mem_1_str6), .col7(screen_mem_1_str7),
    .col8(screen_mem_1_str8), .col9(screen_mem_1_str9), .col10(screen_mem_1_str10),
    .col11(screen_mem_1_str11), .col12(screen_mem_1_str12), .col13(screen_mem_1_str13),
    .col14(screen_mem_1__14), .col15(screen_mem_1_str15), .col16(screen_mem_1_str0_2),
    .col17(screen_mem_1_str1_2), .col18(screen_mem_1_str2_2), .col19(screen_mem_1_str3_2),
    .col20(screen_mem_1_str4_2), .col21(screen_mem_1_str5_2), .col22(screen_mem_1_str6_2),
    .col23(screen_mem_1_str7_2), .col24(screen_mem_1_str8_2), .col25(screen_mem_1_str9_2),
    .col26(screen_mem_1_str10_2), .col27(screen_mem_1_str11_2), .col28(screen_mem_1_str12_2),
    .col29(screen_mem_1_str13_2), .col30(screen_mem_1__14_2), .col31(screen_mem_1_str15_2));
  DotMatrix #(.matrixcols(32), .matrixrows(16)) dotmatrix_2 (
    .col0(screen_mem_2_str0), .col1(screen_mem_2_str1), .col2(screen_mem_2_str2), .col3(screen_mem_2_str3),
    .col4(screen_mem_2_str4), .col5(screen_mem_2_str5), .col6(screen_mem_2_str6), .col7(screen_mem_2_str7),
    .col8(screen_mem_2_str8), .col9(screen_mem_2_str9), .col10(screen_mem_2_str10),
    .col11(screen_mem_2_str11), .col12(screen_mem_2_str12), .col13(screen_mem_2_str13),
    .col14(screen_mem_2__14), .col15(screen_mem_2_str15), .col16(screen_mem_2_str0_2),
    .col17(screen_mem_2_str1_2), .col18(screen_mem_2_str2_2), .col19(screen_mem_2_str3_2),
    .col20(screen_mem_2_str4_2), .col21(screen_mem_2_str5_2), .col22(screen_mem_2_str6_2),
    .col23(screen_mem_2_str7_2), .col24(screen_mem_2_str8_2), .col25(screen_mem_2_str9_2),
    .col26(screen_mem_2_str10_2), .col27(screen_mem_2_str11_2), .col28(screen_mem_2_str12_2),
    .col29(screen_mem_2_str13_2), .col30(screen_mem_2__14_2), .col31(screen_mem_2_str15_2));
  DotMatrix #(.matrixcols(32), .matrixrows(16)) dotmatrix_3 (
    .col0(screen_mem_3_str0), .col1(screen_mem_3_str1), .col2(screen_mem_3_str2), .col3(screen_mem_3_str3),
    .col4(screen_mem_3_str4), .col5(screen_mem_3_str5), .col6(screen_mem_3_str6), .col7(screen_mem_3_str7),
    .col8(screen_mem_3_str8), .col9(screen_mem_3_str9), .col10(screen_mem_3_str10),
    .col11(screen_mem_3_str11), .col12(screen_mem_3_str12), .col13(screen_mem_3_str13),
    .col14(screen_mem_3__14), .col15(screen_mem_3_str15), .col16(screen_mem_3_str0_2),
    .col17(screen_mem_3_str1_2), .col18(screen_mem_3_str2_2), .col19(screen_mem_3_str3_2),
    .col20(screen_mem_3_str4_2), .col21(screen_mem_3_str5_2), .col22(screen_mem_3_str6_2),
    .col23(screen_mem_3_str7_2), .col24(screen_mem_3_str8_2), .col25(screen_mem_3_str9_2),
    .col26(screen_mem_3_str10_2), .col27(screen_mem_3_str11_2), .col28(screen_mem_3_str12_2),
    .col29(screen_mem_3_str13_2), .col30(screen_mem_3__14_2), .col31(screen_mem_3_str15_2));
  DotMatrix #(.matrixcols(32), .matrixrows(16)) dotmatrix_4 (
    .col0(screen_mem_4_str0), .col1(screen_mem_4_str1), .col2(screen_mem_4_str2), .col3(screen_mem_4_str3),
    .col4(screen_mem_4_str4), .col5(screen_mem_4_str5), .col6(screen_mem_4_str6), .col7(screen_mem_4_str7),
    .col8(screen_mem_4_str8), .col9(screen_mem_4_str9), .col10(screen_mem_4_str10),
    .col11(screen_mem_4_str11), .col12(screen_mem_4_str12), .col13(screen_mem_4_str13),
    .col14(screen_mem_4__14), .col15(screen_mem_4_str15), .col16(screen_mem_4_str0_2),
    .col17(screen_mem_4_str1_2), .col18(screen_mem_4_str2_2), .col19(screen_mem_4_str3_2),
    .col20(screen_mem_4_str4_2), .col21(screen_mem_4_str5_2), .col22(screen_mem_4_str6_2),
    .col23(screen_mem_4_str7_2), .col24(screen_mem_4_str8_2), .col25(screen_mem_4_str9_2),
    .col26(screen_mem_4_str10_2), .col27(screen_mem_4_str11_2), .col28(screen_mem_4_str12_2),
    .col29(screen_mem_4_str13_2), .col30(screen_mem_4__14_2), .col31(screen_mem_4_str15_2));
  // Probe on cdm16e_1_p9
  // Probe on cdm16e_1_p9
  // Probe on cdm16e_1_p9
  // Probe on cdm16e_1_p10
  // Probe on cdm16e_1_p10
  // Probe on cdm16e_1_p10
  // RAM ram_1: pin names not known; wires that end beside it: addr, \bit , mem, cl, r_w, data
  screen_mem screen_mem_1 (
    .clock(cl), .data(data), .addr(addr), .start_pos(r1), .str0(screen_mem_1_str0), .str1(screen_mem_1_str1),
    .str2(screen_mem_1_str2), .str3(screen_mem_1_str3), .str4(screen_mem_1_str4), .str5(screen_mem_1_str5),
    .str6(screen_mem_1_str6), .str7(screen_mem_1_str7), .str8(screen_mem_1_str8), .str9(screen_mem_1_str9),
    .str10(screen_mem_1_str10), .str11(screen_mem_1_str11), .str12(screen_mem_1_str12),
    .str13(screen_mem_1_str13), ._14(screen_mem_1__14), .str15(screen_mem_1_str15),
    .str0_2(screen_mem_1_str0_2), .str1_2(screen_mem_1_str1_2), .str2_2(screen_mem_1_str2_2),
    .str3_2(screen_mem_1_str3_2), .str4_2(screen_mem_1_str4_2), .str5_2(screen_mem_1_str5_2),
    .str6_2(screen_mem_1_str6_2), .str7_2(screen_mem_1_str7_2), .str8_2(screen_mem_1_str8_2),
    .str9_2(screen_mem_1_str9_2), .str10_2(screen_mem_1_str10_2), .str11_2(screen_mem_1_str11_2),
    .str12_2(screen_mem_1_str12_2), .str13_2(screen_mem_1_str13_2), ._14_2(screen_mem_1__14_2),
    .str15_2(screen_mem_1_str15_2), .next_pos(screen_mem_1_next_pos), .clock_out(screen_mem_1_clock_out),
    .data_out(screen_mem_1_data_out), .addr_out(screen_mem_1_addr_out));
  screen_mem screen_mem_2 (
    .clock(cl), .data(data), .addr(addr), .start_pos(np1), .str0(screen_mem_2_str0),
    .str1(screen_mem_2_str1), .str2(screen_mem_2_str2), .str3(screen_mem_2_str3), .str4(screen_mem_2_str4),
    .str5(screen_mem_2_str5), .str6(screen_mem_2_str6), .str7(screen_mem_2_str7), .str8(screen_mem_2_str8),
    .str9(screen_mem_2_str9), .str10(screen_mem_2_str10), .str11(screen_mem_2_str11),
    .str12(screen_mem_2_str12), .str13(screen_mem_2_str13), ._14(screen_mem_2__14),
    .str15(screen_mem_2_str15), .str0_2(screen_mem_2_str0_2), .str1_2(screen_mem_2_str1_2),
    .str2_2(screen_mem_2_str2_2), .str3_2(screen_mem_2_str3_2), .str4_2(screen_mem_2_str4_2),
    .str5_2(screen_mem_2_str5_2), .str6_2(screen_mem_2_str6_2), .str7_2(screen_mem_2_str7_2),
    .str8_2(screen_mem_2_str8_2), .str9_2(screen_mem_2_str9_2), .str10_2(screen_mem_2_str10_2),
    .str11_2(screen_mem_2_str11_2), .str12_2(screen_mem_2_str12_2), .str13_2(screen_mem_2_str13_2),
    ._14_2(screen_mem_2__14_2), .str15_2(screen_mem_2_str15_2), .next_pos(screen_mem_2_next_pos),
    .clock_out(screen_mem_2_clock_out), .data_out(screen_mem_2_data_out), .addr_out(screen_mem_2_addr_out));
  screen_mem screen_mem_3 (
    .clock(cl), .data(data), .addr(addr), .start_pos(np2), .str0(screen_mem_3_str0),
    .str1(screen_mem_3_str1), .str2(screen_mem_3_str2), .str3(screen_mem_3_str3), .str4(screen_mem_3_str4),
    .str5(screen_mem_3_str5), .str6(screen_mem_3_str6), .str7(screen_mem_3_str7), .str8(screen_mem_3_str8),
    .str9(screen_mem_3_str9), .str10(screen_mem_3_str10), .str11(screen_mem_3_str11),
    .str12(screen_mem_3_str12), .str13(screen_mem_3_str13), ._14(screen_mem_3__14),
    .str15(screen_mem_3_str15), .str0_2(screen_mem_3_str0_2), .str1_2(screen_mem_3_str1_2),
    .str2_2(screen_mem_3_str2_2), .str3_2(screen_mem_3_str3_2), .str4_2(screen_mem_3_str4_2),
    .str5_2(screen_mem_3_str5_2), .str6_2(screen_mem_3_str6_2), .str7_2(screen_mem_3_str7_2),
    .str8_2(screen_mem_3_str8_2), .str9_2(screen_mem_3_str9_2), .str10_2(screen_mem_3_str10_2),
    .str11_2(screen_mem_3_str11_2), .str12_2(screen_mem_3_str12_2), .str13_2(screen_mem_3_str13_2),
    ._14_2(screen_mem_3__14_2), .str15_2(screen_mem_3_str15_2), .next_pos(screen_mem_3_next_pos),
    .clock_out(screen_mem_3_clock_out), .data_out(screen_mem_3_data_out), .addr_out(screen_mem_3_addr_out));
  screen_mem screen_mem_4 (
    .clock(cl), .data(data), .addr(addr), .start_pos(np3), .str0(screen_mem_4_str0),
    .str1(screen_mem_4_str1), .str2(screen_mem_4_str2), .str3(screen_mem_4_str3), .str4(screen_mem_4_str4),
    .str5(screen_mem_4_str5), .str6(screen_mem_4_str6), .str7(screen_mem_4_str7), .str8(screen_mem_4_str8),
    .str9(screen_mem_4_str9), .str10(screen_mem_4_str10), .str11(screen_mem_4_str11),
    .str12(screen_mem_4_str12), .str13(screen_mem_4_str13), ._14(screen_mem_4__14),
    .str15(screen_mem_4_str15), .str0_2(screen_mem_4_str0_2), .str1_2(screen_mem_4_str1_2),
    .str2_2(screen_mem_4_str2_2), .str3_2(screen_mem_4_str3_2), .str4_2(screen_mem_4_str4_2),
    .str5_2(screen_mem_4_str5_2), .str6_2(screen_mem_4_str6_2), .str7_2(screen_mem_4_str7_2),
    .str8_2(screen_mem_4_str8_2), .str9_2(screen_mem_4_str9_2), .str10_2(screen_mem_4_str10_2),
    .str11_2(screen_mem_4_str11_2), .str12_2(screen_mem_4_str12_2), .str13_2(screen_mem_4_str13_2),
    ._14_2(screen_mem_4__14_2), .str15_2(screen_mem_4_str15_2), .next_pos(screen_mem_4_next_pos),
    .clock_out(screen_mem_4_clock_out), .data_out(screen_mem_4_data_out), .addr_out(screen_mem_4_addr_out));
  // Probe on cdm16e_1_p11
  // Probe on cdm16e_1_p11
  // Probe on cdm16e_1_p11
  // Probe on cdm16e_1_p12
  // Probe on cdm16e_1_p12
  // Probe on cdm16e_1_p12
  DotMatrix #(.matrixcols(32), .matrixrows(16)) dotmatrix_5 (
    .col0(screen_mem_5_str0), .col1(screen_mem_5_str1), .col2(screen_mem_5_str2), .col3(screen_mem_5_str3),
    .col4(screen_mem_5_str4), .col5(screen_mem_5_str5), .col6(screen_mem_5_str6), .col7(screen_mem_5_str7),
    .col8(screen_mem_5_str8), .col9(screen_mem_5_str9), .col10(screen_mem_5_str10),
    .col11(screen_mem_5_str11), .col12(screen_mem_5_str12), .col13(screen_mem_5_str13),
    .col14(screen_mem_5__14), .col15(screen_mem_5_str15), .col16(screen_mem_5_str0_2),
    .col17(screen_mem_5_str1_2), .col18(screen_mem_5_str2_2), .col19(screen_mem_5_str3_2),
    .col20(screen_mem_5_str4_2), .col21(screen_mem_5_str5_2), .col22(screen_mem_5_str6_2),
    .col23(screen_mem_5_str7_2), .col24(screen_mem_5_str8_2), .col25(screen_mem_5_str9_2),
    .col26(screen_mem_5_str10_2), .col27(screen_mem_5_str11_2), .col28(screen_mem_5_str12_2),
    .col29(screen_mem_5_str13_2), .col30(screen_mem_5__14_2), .col31(screen_mem_5_str15_2));
  DotMatrix #(.matrixcols(32), .matrixrows(16)) dotmatrix_6 (
    .col0(screen_mem_6_str0), .col1(screen_mem_6_str1), .col2(screen_mem_6_str2), .col3(screen_mem_6_str3),
    .col4(screen_mem_6_str4), .col5(screen_mem_6_str5), .col6(screen_mem_6_str6), .col7(screen_mem_6_str7),
    .col8(screen_mem_6_str8), .col9(screen_mem_6_str9), .col10(screen_mem_6_str10),
    .col11(screen_mem_6_str11), .col12(screen_mem_6_str12), .col13(screen_mem_6_str13),
    .col14(screen_mem_6__14), .col15(screen_mem_6_str15), .col16(screen_mem_6_str0_2),
    .col17(screen_mem_6_str1_2), .col18(screen_mem_6_str2_2), .col19(screen_mem_6_str3_2),
    .col20(screen_mem_6_str4_2), .col21(screen_mem_6_str5_2), .col22(screen_mem_6_str6_2),
    .col23(screen_mem_6_str7_2), .col24(screen_mem_6_str8_2), .col25(screen_mem_6_str9_2),
    .col26(screen_mem_6_str10_2), .col27(screen_mem_6_str11_2), .col28(screen_mem_6_str12_2),
    .col29(screen_mem_6_str13_2), .col30(screen_mem_6__14_2), .col31(screen_mem_6_str15_2));
  DotMatrix #(.matrixcols(32), .matrixrows(16)) dotmatrix_7 (
    .col0(screen_mem_7_str0), .col1(screen_mem_7_str1), .col2(screen_mem_7_str2), .col3(screen_mem_7_str3),
    .col4(screen_mem_7_str4), .col5(screen_mem_7_str5), .col6(screen_mem_7_str6), .col7(screen_mem_7_str7),
    .col8(screen_mem_7_str8), .col9(screen_mem_7_str9), .col10(screen_mem_7_str10),
    .col11(screen_mem_7_str11), .col12(screen_mem_7_str12), .col13(screen_mem_7_str13),
    .col14(screen_mem_7__14), .col15(screen_mem_7_str15), .col16(screen_mem_7_str0_2),
    .col17(screen_mem_7_str1_2), .col18(screen_mem_7_str2_2), .col19(screen_mem_7_str3_2),
    .col20(screen_mem_7_str4_2), .col21(screen_mem_7_str5_2), .col22(screen_mem_7_str6_2),
    .col23(screen_mem_7_str7_2), .col24(screen_mem_7_str8_2), .col25(screen_mem_7_str9_2),
    .col26(screen_mem_7_str10_2), .col27(screen_mem_7_str11_2), .col28(screen_mem_7_str12_2),
    .col29(screen_mem_7_str13_2), .col30(screen_mem_7__14_2), .col31(screen_mem_7_str15_2));
  DotMatrix #(.matrixcols(32), .matrixrows(16)) dotmatrix_8 (
    .col0(screen_mem_8_str0), .col1(screen_mem_8_str1), .col2(screen_mem_8_str2), .col3(screen_mem_8_str3),
    .col4(screen_mem_8_str4), .col5(screen_mem_8_str5), .col6(screen_mem_8_str6), .col7(screen_mem_8_str7),
    .col8(screen_mem_8_str8), .col9(screen_mem_8_str9), .col10(screen_mem_8_str10),
    .col11(screen_mem_8_str11), .col12(screen_mem_8_str12), .col13(screen_mem_8_str13),
    .col14(screen_mem_8__14), .col15(screen_mem_8_str15), .col16(screen_mem_8_str0_2),
    .col17(screen_mem_8_str1_2), .col18(screen_mem_8_str2_2), .col19(screen_mem_8_str3_2),
    .col20(screen_mem_8_str4_2), .col21(screen_mem_8_str5_2), .col22(screen_mem_8_str6_2),
    .col23(screen_mem_8_str7_2), .col24(screen_mem_8_str8_2), .col25(screen_mem_8_str9_2),
    .col26(screen_mem_8_str10_2), .col27(screen_mem_8_str11_2), .col28(screen_mem_8_str12_2),
    .col29(screen_mem_8_str13_2), .col30(screen_mem_8__14_2), .col31(screen_mem_8_str15_2));
  // Probe on cdm16e_1_p13
  // Probe on cdm16e_1_p13
  // Probe on cdm16e_1_p13
  screen_mem screen_mem_5 (
    .clock(screen_mem_1_clock_out), .data(screen_mem_1_data_out), .addr(screen_mem_1_addr_out),
    .start_pos(screen_mem_1_next_pos), .str0(screen_mem_5_str0), .str1(screen_mem_5_str1),
    .str2(screen_mem_5_str2), .str3(screen_mem_5_str3), .str4(screen_mem_5_str4), .str5(screen_mem_5_str5),
    .str6(screen_mem_5_str6), .str7(screen_mem_5_str7), .str8(screen_mem_5_str8), .str9(screen_mem_5_str9),
    .str10(screen_mem_5_str10), .str11(screen_mem_5_str11), .str12(screen_mem_5_str12),
    .str13(screen_mem_5_str13), ._14(screen_mem_5__14), .str15(screen_mem_5_str15),
    .str0_2(screen_mem_5_str0_2), .str1_2(screen_mem_5_str1_2), .str2_2(screen_mem_5_str2_2),
    .str3_2(screen_mem_5_str3_2), .str4_2(screen_mem_5_str4_2), .str5_2(screen_mem_5_str5_2),
    .str6_2(screen_mem_5_str6_2), .str7_2(screen_mem_5_str7_2), .str8_2(screen_mem_5_str8_2),
    .str9_2(screen_mem_5_str9_2), .str10_2(screen_mem_5_str10_2), .str11_2(screen_mem_5_str11_2),
    .str12_2(screen_mem_5_str12_2), .str13_2(screen_mem_5_str13_2), ._14_2(screen_mem_5__14_2),
    .str15_2(screen_mem_5_str15_2), .next_pos(np1));  // open: clock_out, data_out, addr_out
  screen_mem screen_mem_6 (
    .clock(screen_mem_2_clock_out), .data(screen_mem_2_data_out), .addr(screen_mem_2_addr_out),
    .start_pos(screen_mem_2_next_pos), .str0(screen_mem_6_str0), .str1(screen_mem_6_str1),
    .str2(screen_mem_6_str2), .str3(screen_mem_6_str3), .str4(screen_mem_6_str4), .str5(screen_mem_6_str5),
    .str6(screen_mem_6_str6), .str7(screen_mem_6_str7), .str8(screen_mem_6_str8), .str9(screen_mem_6_str9),
    .str10(screen_mem_6_str10), .str11(screen_mem_6_str11), .str12(screen_mem_6_str12),
    .str13(screen_mem_6_str13), ._14(screen_mem_6__14), .str15(screen_mem_6_str15),
    .str0_2(screen_mem_6_str0_2), .str1_2(screen_mem_6_str1_2), .str2_2(screen_mem_6_str2_2),
    .str3_2(screen_mem_6_str3_2), .str4_2(screen_mem_6_str4_2), .str5_2(screen_mem_6_str5_2),
    .str6_2(screen_mem_6_str6_2), .str7_2(screen_mem_6_str7_2), .str8_2(screen_mem_6_str8_2),
    .str9_2(screen_mem_6_str9_2), .str10_2(screen_mem_6_str10_2), .str11_2(screen_mem_6_str11_2),
    .str12_2(screen_mem_6_str12_2), .str13_2(screen_mem_6_str13_2), ._14_2(screen_mem_6__14_2),
    .str15_2(screen_mem_6_str15_2), .next_pos(np2));  // open: clock_out, data_out, addr_out
  screen_mem screen_mem_7 (
    .clock(screen_mem_3_clock_out), .data(screen_mem_3_data_out), .addr(screen_mem_3_addr_out),
    .start_pos(screen_mem_3_next_pos), .str0(screen_mem_7_str0), .str1(screen_mem_7_str1),
    .str2(screen_mem_7_str2), .str3(screen_mem_7_str3), .str4(screen_mem_7_str4), .str5(screen_mem_7_str5),
    .str6(screen_mem_7_str6), .str7(screen_mem_7_str7), .str8(screen_mem_7_str8), .str9(screen_mem_7_str9),
    .str10(screen_mem_7_str10), .str11(screen_mem_7_str11), .str12(screen_mem_7_str12),
    .str13(screen_mem_7_str13), ._14(screen_mem_7__14), .str15(screen_mem_7_str15),
    .str0_2(screen_mem_7_str0_2), .str1_2(screen_mem_7_str1_2), .str2_2(screen_mem_7_str2_2),
    .str3_2(screen_mem_7_str3_2), .str4_2(screen_mem_7_str4_2), .str5_2(screen_mem_7_str5_2),
    .str6_2(screen_mem_7_str6_2), .str7_2(screen_mem_7_str7_2), .str8_2(screen_mem_7_str8_2),
    .str9_2(screen_mem_7_str9_2), .str10_2(screen_mem_7_str10_2), .str11_2(screen_mem_7_str11_2),
    .str12_2(screen_mem_7_str12_2), .str13_2(screen_mem_7_str13_2), ._14_2(screen_mem_7__14_2),
    .str15_2(screen_mem_7_str15_2), .next_pos(np3));  // open: clock_out, data_out, addr_out
  screen_mem screen_mem_8 (
    .clock(screen_mem_4_clock_out), .data(screen_mem_4_data_out), .addr(screen_mem_4_addr_out),
    .start_pos(screen_mem_4_next_pos), .str0(screen_mem_8_str0), .str1(screen_mem_8_str1),
    .str2(screen_mem_8_str2), .str3(screen_mem_8_str3), .str4(screen_mem_8_str4), .str5(screen_mem_8_str5),
    .str6(screen_mem_8_str6), .str7(screen_mem_8_str7), .str8(screen_mem_8_str8), .str9(screen_mem_8_str9),
    .str10(screen_mem_8_str10), .str11(screen_mem_8_str11), .str12(screen_mem_8_str12),
    .str13(screen_mem_8_str13), ._14(screen_mem_8__14), .str15(screen_mem_8_str15),
    .str0_2(screen_mem_8_str0_2), .str1_2(screen_mem_8_str1_2), .str2_2(screen_mem_8_str2_2),
    .str3_2(screen_mem_8_str3_2), .str4_2(screen_mem_8_str4_2), .str5_2(screen_mem_8_str5_2),
    .str6_2(screen_mem_8_str6_2), .str7_2(screen_mem_8_str7_2), .str8_2(screen_mem_8_str8_2),
    .str9_2(screen_mem_8_str9_2), .str10_2(screen_mem_8_str10_2), .str11_2(screen_mem_8_str11_2),
    .str12_2(screen_mem_8_str12_2), .str13_2(screen_mem_8_str13_2), ._14_2(screen_mem_8__14_2),
    .str15_2(screen_mem_8_str15_2));  // open: next_pos, clock_out, data_out, addr_out
endmodule

module data_sel (
  input  [15:0] out,
  input  r_w,
  input  [15:0] in,
  output [15:0] data
);

  wire not_1_out;

  assign data = not_1_out ? out : 16'bz;  // Controlled_Buffer controlled_buffer_1
  not not_1 (not_1_out, r_w);
  assign in = r_w ? data : 16'bz;  // Controlled_Buffer controlled_buffer_2
endmodule

module gpu_str_mem (
  input  [15:0] data,
  input  [15:0] addr,
  input  clock,
  input  [15:0] pos,
  output [15:0] str,
  output [15:0] pos_next
);

  wire comparator_1_eq;
  wire [15:0] multiplexer_1_out;

  Comparator #(.width(16), .mode("unsigned")) comparator_1 (.a(addr), .b(pos), .eq(comparator_1_eq));  // open: gt, lt
  Adder #(.width(16)) adder_1 (.a(pos), .b(16'h2), .out(pos_next));  // open: cin, cout
  Multiplexer #(.width(16)) multiplexer_1 (
    .in0(str), .in1(data), .out(multiplexer_1_out), .sel(comparator_1_eq));  // open: en
  Register #(.width(16)) register_1 (.D(multiplexer_1_out), .Q(str), .clk(clock));  // open: en, clr
endmodule

module screen_mem (
  input  [15:0] data,
  input  [15:0] addr,
  input  clock,
  input  [15:0] start_pos,
  output [15:0] str0,
  output [15:0] str1,
  output [15:0] str2,
  output [15:0] str3,
  output [15:0] str4,
  output [15:0] str5,
  output [15:0] str6,
  output [15:0] str7,
  output [15:0] str8,
  output [15:0] str9,
  output [15:0] str10,
  output [15:0] str11,
  output [15:0] str12,
  output [15:0] str13,
  output [15:0] _14,
  output [15:0] str15,
  output [15:0] str0_2,
  output [15:0] str1_2,
  output [15:0] str2_2,
  output [15:0] str3_2,
  output [15:0] str4_2,
  output [15:0] str5_2,
  output [15:0] str6_2,
  output [15:0] str7_2,
  output [15:0] str8_2,
  output [15:0] str9_2,
  output [15:0] str10_2,
  output [15:0] str11_2,
  output [15:0] str12_2,
  output [15:0] str13_2,
  output [15:0] _14_2,
  output [15:0] str15_2,
  output [15:0] data_out,
  output clock_out,
  output [15:0] addr_out,
  output [15:0] next_pos
);

  wire [15:0] gpu_str_mem_1_pos_next, gpu_str_mem_2_pos_next, gpu_str_mem_3_pos_next, gpu_str_mem_4_pos_next,
       gpu_str_mem_5_pos_next, gpu_str_mem_6_pos_next, gpu_str_mem_7_pos_next, gpu_str_mem_8_pos_next,
       gpu_str_mem_9_pos_next, gpu_str_mem_10_pos_next, gpu_str_mem_11_pos_next, gpu_str_mem_12_pos_next,
       gpu_str_mem_13_pos_next, gpu_str_mem_14_pos_next, gpu_str_mem_15_pos_next, gpu_str_mem_16_pos_next,
       gpu_str_mem_17_pos_next, gpu_str_mem_18_pos_next, gpu_str_mem_19_pos_next, gpu_str_mem_20_pos_next,
       gpu_str_mem_21_pos_next, gpu_str_mem_22_pos_next, gpu_str_mem_23_pos_next, gpu_str_mem_24_pos_next,
       gpu_str_mem_25_pos_next, gpu_str_mem_26_pos_next, gpu_str_mem_27_pos_next, gpu_str_mem_28_pos_next,
       gpu_str_mem_29_pos_next, gpu_str_mem_30_pos_next, gpu_str_mem_31_pos_next;

  gpu_str_mem gpu_str_mem_1 (
    .data(data), .addr(addr), .str(str0), .pos(start_pos), .clock(clock), .pos_next(gpu_str_mem_1_pos_next));
  gpu_str_mem gpu_str_mem_2 (
    .data(data), .addr(addr), .str(str1), .pos(gpu_str_mem_1_pos_next), .clock(clock),
    .pos_next(gpu_str_mem_2_pos_next));
  gpu_str_mem gpu_str_mem_3 (
    .data(data), .addr(addr), .str(str2), .pos(gpu_str_mem_2_pos_next), .clock(clock),
    .pos_next(gpu_str_mem_3_pos_next));
  gpu_str_mem gpu_str_mem_4 (
    .data(data), .addr(addr), .str(str3), .pos(gpu_str_mem_3_pos_next), .clock(clock),
    .pos_next(gpu_str_mem_4_pos_next));
  gpu_str_mem gpu_str_mem_5 (
    .data(data), .addr(addr), .str(str4), .pos(gpu_str_mem_4_pos_next), .clock(clock),
    .pos_next(gpu_str_mem_5_pos_next));
  gpu_str_mem gpu_str_mem_6 (
    .data(data), .addr(addr), .str(str5), .pos(gpu_str_mem_5_pos_next), .clock(clock),
    .pos_next(gpu_str_mem_6_pos_next));
  gpu_str_mem gpu_str_mem_7 (
    .data(data), .addr(addr), .str(str6), .pos(gpu_str_mem_6_pos_next), .clock(clock),
    .pos_next(gpu_str_mem_7_pos_next));
  gpu_str_mem gpu_str_mem_8 (
    .data(data), .addr(addr), .str(str8), .pos(gpu_str_mem_9_pos_next), .clock(clock),
    .pos_next(gpu_str_mem_8_pos_next));
  gpu_str_mem gpu_str_mem_9 (
    .data(data), .addr(addr), .str(str7), .pos(gpu_str_mem_7_pos_next), .clock(clock),
    .pos_next(gpu_str_mem_9_pos_next));
  gpu_str_mem gpu_str_mem_10 (
    .data(data), .addr(addr), .str(str9), .pos(gpu_str_mem_8_pos_next), .clock(clock),
    .pos_next(gpu_str_mem_10_pos_next));
  gpu_str_mem gpu_str_mem_11 (
    .data(data), .addr(addr), .str(str11), .pos(gpu_str_mem_12_pos_next), .clock(clock),
    .pos_next(gpu_str_mem_11_pos_next));
  gpu_str_mem gpu_str_mem_12 (
    .data(data), .addr(addr), .str(str10), .pos(gpu_str_mem_10_pos_next), .clock(clock),
    .pos_next(gpu_str_mem_12_pos_next));
  gpu_str_mem gpu_str_mem_13 (
    .data(data), .addr(addr), .str(str12), .pos(gpu_str_mem_11_pos_next), .clock(clock),
    .pos_next(gpu_str_mem_13_pos_next));
  gpu_str_mem gpu_str_mem_14 (
    .data(data), .addr(addr), .str(str13), .pos(gpu_str_mem_13_pos_next), .clock(clock),
    .pos_next(gpu_str_mem_14_pos_next));
  gpu_str_mem gpu_str_mem_15 (
    .data(data), .addr(addr), .str(str15), .pos(gpu_str_mem_16_pos_next), .clock(clock),
    .pos_next(gpu_str_mem_15_pos_next));
  gpu_str_mem gpu_str_mem_16 (
    .data(data), .addr(addr), .str(_14), .pos(gpu_str_mem_14_pos_next), .clock(clock),
    .pos_next(gpu_str_mem_16_pos_next));
  gpu_str_mem gpu_str_mem_17 (
    .data(data), .addr(addr), .str(str0_2), .pos(gpu_str_mem_15_pos_next), .clock(clock),
    .pos_next(gpu_str_mem_17_pos_next));
  gpu_str_mem gpu_str_mem_18 (
    .data(data), .addr(addr), .str(str3_2), .pos(gpu_str_mem_19_pos_next), .clock(clock),
    .pos_next(gpu_str_mem_18_pos_next));
  gpu_str_mem gpu_str_mem_19 (
    .data(data), .addr(addr), .str(str2_2), .pos(gpu_str_mem_20_pos_next), .clock(clock),
    .pos_next(gpu_str_mem_19_pos_next));
  gpu_str_mem gpu_str_mem_20 (
    .data(data), .addr(addr), .str(str1_2), .pos(gpu_str_mem_17_pos_next), .clock(clock),
    .pos_next(gpu_str_mem_20_pos_next));
  gpu_str_mem gpu_str_mem_21 (
    .data(data), .addr(addr), .str(str5_2), .pos(gpu_str_mem_22_pos_next), .clock(clock),
    .pos_next(gpu_str_mem_21_pos_next));
  gpu_str_mem gpu_str_mem_22 (
    .data(data), .addr(addr), .str(str4_2), .pos(gpu_str_mem_18_pos_next), .clock(clock),
    .pos_next(gpu_str_mem_22_pos_next));
  gpu_str_mem gpu_str_mem_23 (
    .data(data), .addr(addr), .str(str7_2), .pos(gpu_str_mem_25_pos_next), .clock(clock),
    .pos_next(gpu_str_mem_23_pos_next));
  gpu_str_mem gpu_str_mem_24 (
    .data(data), .addr(addr), .str(str8_2), .pos(gpu_str_mem_23_pos_next), .clock(clock),
    .pos_next(gpu_str_mem_24_pos_next));
  gpu_str_mem gpu_str_mem_25 (
    .data(data), .addr(addr), .str(str6_2), .pos(gpu_str_mem_21_pos_next), .clock(clock),
    .pos_next(gpu_str_mem_25_pos_next));
  gpu_str_mem gpu_str_mem_26 (
    .data(data), .addr(addr), .str(str10_2), .pos(gpu_str_mem_28_pos_next), .clock(clock),
    .pos_next(gpu_str_mem_26_pos_next));
  gpu_str_mem gpu_str_mem_27 (
    .data(data), .addr(addr), .str(str11_2), .pos(gpu_str_mem_26_pos_next), .clock(clock),
    .pos_next(gpu_str_mem_27_pos_next));
  gpu_str_mem gpu_str_mem_28 (
    .data(data), .addr(addr), .str(str9_2), .pos(gpu_str_mem_24_pos_next), .clock(clock),
    .pos_next(gpu_str_mem_28_pos_next));
  gpu_str_mem gpu_str_mem_29 (
    .data(data), .addr(addr), .str(str12_2), .pos(gpu_str_mem_27_pos_next), .clock(clock),
    .pos_next(gpu_str_mem_29_pos_next));
  gpu_str_mem gpu_str_mem_30 (
    .data(data), .addr(addr), .str(str13_2), .pos(gpu_str_mem_29_pos_next), .clock(clock),
    .pos_next(gpu_str_mem_30_pos_next));
  gpu_str_mem gpu_str_mem_31 (
    .data(data), .addr(addr), .str(_14_2), .pos(gpu_str_mem_30_pos_next), .clock(clock),
    .pos_next(gpu_str_mem_31_pos_next));
  gpu_str_mem gpu_str_mem_32 (
    .data(data), .addr(addr), .str(str15_2), .pos(gpu_str_mem_31_pos_next), .clock(clock), .pos_next(next_pos));

  assign addr_out = addr;
  assign clock_out = clock;
  assign data_out = data;
endmodule

module cu (
  input  \cell ,
  input  [7:0] neighbors,
  output new_gen
);

  wire comparator_1_eq, comparator_2_eq, or_1_out;
  wire [3:0] bitadder_1_out;

  BitAdder bitadder_1 (.in0(neighbors), .out(bitadder_1_out));
  Comparator #(.width(4), .mode("unsigned")) comparator_1 (
    .a(bitadder_1_out), .b(4'b0011), .eq(comparator_1_eq));  // open: gt, lt
  Comparator #(.width(4), .mode("unsigned")) comparator_2 (
    .a(bitadder_1_out), .b(4'b0010), .eq(comparator_2_eq));  // open: gt, lt
  or or_1 (or_1_out, comparator_1_eq, comparator_2_eq);
  Multiplexer multiplexer_1 (.in0(comparator_1_eq), .in1(or_1_out), .out(new_gen), .en(\cell ));  // open: sel
endmodule
